# Fritzing sketch sonic_rangefinder (saved by Fritzing 0.9.6b)
breadboards: 1

parts:
  Pi1 = Adafruit Pi Cobbler
  HC-SR04_Sensor_1 = HC-SR04 Ultrasonic Distance Sensor
  R1 = Resistor [tolerance=±5% resistance=1k package="0805 [SMD]"]
  R2 = Resistor [tolerance=±5% resistance=1k package="0805 [SMD]"]
  R3 = Resistor [tolerance=±5% resistance=1k package="0805 [SMD]"]

nets:
  N1: Pi1.5V0, HC-SR04_Sensor_1.VCC
  GND: Pi1.GND, HC-SR04_Sensor_1.GND, R3.Pin_1
  N2: Pi1.MOSI, HC-SR04_Sensor_1.TRIG
  N3: Pi1.SCLK, R1.Pin_0, R2.Pin_0
  N4: HC-SR04_Sensor_1.ECHO, R1.Pin_1
  N5: R2.Pin_1, R3.Pin_0

custom parts:
  Adafruit Pi Cobbler: Adafruit Pi Cobbler GPIO Breakout for Raspberry Pi
