# Fritzing sketch 07.PotMeters (saved by Fritzing 0.9.6b)
breadboards: 1

parts:
  Part1 = Arduino Uno (Rev3)
  U1 = POT [package=pot_mammoth]
  U2 = POT [package=pot_mammoth]

nets:
  N1: Part1.A0, U2.A
  N2: Part1.A1, U1.A
  N3: Part1.5V, U1.E, U2.E
  N4: Part1.GND, U1.S, U2.S
